# Fritzing sketch 3DLidarScanner-v2 (saved by Fritzing 0.9.10b)
breadboards: 1

parts:
  Part1 = Arduino Uno (Rev3)
  Pololu_A1 = Pololu A4988 [package=SO16]
  Pololu_A2 = Pololu A4988 [package=SO16]
  M1 = Stepper Motor - Bipolar
  Power_plug1 = Power plug
  M2 = Stepper Motor - Bipolar
  C1 = Electrolytic Capacitor [capacitance=1µF voltage=35V package="100 mil [THT, electrolytic]"]

nets:
  N1: Part1.D8, Pololu_A1.ENABLE, Pololu_A2.ENABLE
  N2: Part1.D2, Pololu_A2.DIR
  N3: Part1.D3_PWM, Pololu_A1.DIR
  N4: Part1.D5_PWM, Pololu_A2.STEP
  N5: Part1.D6_PWM, Pololu_A1.STEP
  5V: Part1.5V, Pololu_A2.VDD
  N6: Part1.GND, Pololu_A2.GND#8
  N7: Pololu_A1.1B, M2.D
  N8: Pololu_A1.1A, M2.B
  N9: Pololu_A1.2A, M2.C
  N10: Pololu_A1.GND#14, Pololu_A2.GND#14, Power_plug1.GND, C1.-
  N11: Pololu_A1.VMOT, Pololu_A2.VMOT, Power_plug1.VCC, C1.+
  N12: Pololu_A2.1B, M1.D
  N13: Pololu_A2.1A, M1.B
  N14: Pololu_A2.2A, M1.C
  N15: Pololu_A2.2B, M1.A
